# Fritzing sketch twerk (saved by Fritzing 0.9.2b)
breadboards: 1

parts:
  Part1 = Arduino Uno (Rev3)
  Part2 = Tri-Axis Gyro Breakout - L3G4200D

nets:
  N1: Part1.A4/SDA, Part2.SDA
  N2: Part1.A5/SCL, Part2.SCL
  N3: Part1.D2, Part2.INT1
  3V3: Part1.3V3, Part2.VCC
  GND: Part1.GND, Part2.GND
